# Fritzing sketch arduino esp8266 web (saved by Fritzing 0.9.3b)

parts:
  U1 = ESP8266 WiFi Module [part_number=ESP8266]
  Part1 = Arduino Uno (Rev3)
  R2 = Resistor [tolerance=±5% resistance=470 package=THT]
  R1 = Resistor [tolerance=±5% resistance=330 package=THT]
  Part2 = Arduino Uno (Rev3)
  R2_2 = Resistor [tolerance=±5% resistance=470 package=THT]
  U2 = ESP8266 WiFi Module [part_number=ESP8266]
  R1_2 = Resistor [tolerance=±5% resistance=330 package=THT]
  DS1 = DS18B20 1-Wire Temperature Sensor [part_number=DS18B20]
  DS2 = DS18B20 1-Wire Temperature Sensor [part_number=DS18B20]  # not connected
  DS3 = DS18B20 1-Wire Temperature Sensor [part_number=DS18B20]  # not connected
  DS4 = DS18B20 1-Wire Temperature Sensor [part_number=DS18B20]  # not connected
  DS5 = DS18B20 1-Wire Temperature Sensor [part_number=DS18B20]  # not connected
  DS6 = DS18B20 1-Wire Temperature Sensor [part_number=DS18B20]  # not connected
  R3 = Resistor [tolerance=±5% resistance=470 package=THT]

nets:
  N1: U1.RXD, R2.Pin_0, R1.Pin_0
  N2: U1.GPIO_0, U1.GND, R1.Pin_1
  N3: U1.CH_PD, Part1.3V3
  N4: U1.TXD, Part1.D1/TX
  N5: Part1.D0/RX, R2.Pin_1
  N6: Part2.D10_PWM/SS, U2.TXD
  N7: Part2.D11_PWM/MOSI, R2_2.Pin_1
  GND: Part2.GND, DS1.GND
  N8: Part2.D2, DS1.DQ
  N9: Part2.3V3, U2.CH_PD
  N10: Part2.5V, R3.Pin_0
  N11: R2_2.Pin_0, U2.RXD, R1_2.Pin_0
  N12: U2.GND, R1_2.Pin_1
  N13: DS1.VDD, R3.Pin_1

notes:
  Rangkaian upload program ESP8266
  Rangkaian upload program arduino uno

custom parts:
  ESP8266 WiFi Module: Generic WiFi Module based on the ESP8266 with onboard PCB antenna and UART communications
